// Logisim project exercise3.circ as structural Verilog: 1 circuit, main circuit main
module main (
  input  in_1
);

  wire clock_1_out, j_k_ff_1_q, j_k_ff_2_q, j_k_ff_2_qn, nand_1_out, nand_2_out, nand_3_out, nand_4_out,
       not_1_out, not_2_out, undriven;

  not not_1 (not_1_out, in_1);
  nand nand_1 (nand_1_out, j_k_ff_2_qn, not_1_out);
  not not_2 (not_2_out, nand_1_out);
  Clock clock_1 (.out(clock_1_out));
  J_K_Flip_Flop j_k_ff_1 (
    .J(not_2_out), .clk(clock_1_out), .K(in_1), .Q(j_k_ff_1_q), .en(undriven), .reset(undriven));  // open: Qn, preset
  J_K_Flip_Flop j_k_ff_2 (
    .J(in_1), .clk(clock_1_out), .K(in_1), .Q(j_k_ff_2_q), .Qn(j_k_ff_2_qn));  // open: preset, en, reset
  nand nand_2 (nand_2_out, j_k_ff_2_q, in_1);
  nand nand_3 (nand_3_out, j_k_ff_1_q, not_1_out);
  LED led_1 (.in(nand_4_out));
  nand nand_4 (nand_4_out, nand_2_out, nand_3_out);
endmodule
