// Logisim project exercise5.circ as structural Verilog: 1 circuit, main circuit main
module main (
  input  in_1
);

  wire clock_1_out, d_ff_1_q, d_ff_1_qn, j_k_ff_1_q, nand_1_out, nand_2_out, nand_3_out, nand_4_out,
       nand_5_out, not_1_out, not_2_out, not_3_out;

  not not_1 (not_1_out, in_1);
  nand nand_1 (nand_1_out, d_ff_1_q, not_1_out);
  nand nand_2 (nand_2_out, not_1_out, d_ff_1_qn);
  nand nand_3 (nand_3_out, in_1, d_ff_1_q);
  not not_2 (not_2_out, nand_1_out);
  nand nand_4 (nand_4_out, nand_2_out, nand_3_out);
  Clock clock_1 (.out(clock_1_out));
  J_K_Flip_Flop j_k_ff_1 (
    .J(not_2_out), .clk(clock_1_out), .K(nand_4_out), .Q(j_k_ff_1_q));  // open: Qn, preset, en, reset
  D_Flip_Flop d_ff_1 (.clk(clock_1_out), .D(in_1), .Q(d_ff_1_q), .Qn(d_ff_1_qn));  // open: preset, en, reset
  nand nand_5 (nand_5_out, j_k_ff_1_q, d_ff_1_q);
  LED led_1 (.in(j_k_ff_1_q));
  LED led_2 (.in(d_ff_1_q));
  not not_3 (not_3_out, nand_5_out);
  LED led_3 (.in(not_3_out));

  // Notes on the sheet:
  //   JK1
  //   D0
endmodule
